// Logisim project MIPS_DATAPATH.circ as structural Verilog: 6 circuits, main circuit main
module main (
);

  _22_BIT_REGISTER u_22_bit_register_1 ();  // open: READ_DATA_1, READ_DATA_2, WRITE_REGISTER, WRITE_CONTROL, DATA_WRITE, CLOCK, CLEAR, DATA_REGISTER_1, DATA_REGISTER_2
  _22_BIT_ALU u_22_bit_alu_1 ();  // open: in_3, in_5, add_ovf, sub_ovf, OUT, A, B, BEQ, BNE, in_4
  CONTROL_UNIT control_unit_1 ();  // open: OPCODE, Reg_Dest, Reg_Write, MEMRead, MEMWrite, Mem_To_Reg, Jump, Branch, ALUOP, ALU_SRC

  // Notes on the sheet:
  //   22 BIT REGISTER 
  //   22 BIT ALU
  //   CONTROL UNIT
endmodule

module _22_BIT_REGISTER (
  input  [4:0] DATA_REGISTER_1,
  input  [4:0] WRITE_REGISTER,
  input  [4:0] DATA_REGISTER_2,
  input  WRITE_CONTROL,
  input  CLOCK,
  input  CLEAR,
  input  [21:0] DATA_WRITE,
  output [21:0] READ_DATA_1,
  output [21:0] READ_DATA_2
);

  wire and_1_out, and_2_out, and_3_out, and_4_out, and_5_out, and_6_out, and_7_out, and_8_out, and_9_out,
       and_10_out, and_11_out, and_12_out, and_13_out, and_14_out, and_15_out, and_16_out, and_17_out,
       and_18_out, and_19_out, and_20_out, and_21_out, and_22_out, decoder_1_out0, decoder_1_out1,
       decoder_1_out2, decoder_1_out3, decoder_1_out4, decoder_1_out5, decoder_1_out6, decoder_1_out7,
       decoder_1_out8, decoder_1_out9, decoder_1_out10, decoder_1_out11, decoder_1_out12, decoder_1_out13,
       decoder_1_out14, decoder_1_out15, decoder_1_out16, decoder_1_out17, decoder_1_out18, decoder_1_out19,
       decoder_1_out20, decoder_1_out21;
  wire [21:0] _0_q, _1_q, _2_q, _3_q, _4_q, _5_q, _6_q, _7_q, _8_q, _9_q, _10_q, _11_q, _12_q, _13_q, _14_q,
       _15_q, _16_q, _17_q, _18_q, _19_q, _20_q, _21_q;

  Decoder #(.select(5), .enable("false")) decoder_1 (
    .out0(decoder_1_out0), .out1(decoder_1_out1), .out2(decoder_1_out2), .out3(decoder_1_out3),
    .out4(decoder_1_out4), .out5(decoder_1_out5), .out6(decoder_1_out6), .out7(decoder_1_out7),
    .out8(decoder_1_out8), .out9(decoder_1_out9), .out10(decoder_1_out10), .out11(decoder_1_out11),
    .out12(decoder_1_out12), .out13(decoder_1_out13), .out14(decoder_1_out14), .out15(decoder_1_out15),
    .out16(decoder_1_out16), .out17(decoder_1_out17), .out18(decoder_1_out18), .out19(decoder_1_out19),
    .out20(decoder_1_out20), .out21(decoder_1_out21), .sel(WRITE_REGISTER));  // open: out22, out23, out24, out25, out26, out27, out28, out29, out30, out31
  Register #(.width(22)) _0 (.D(DATA_WRITE), .en(and_1_out), .Q(_0_q), .clk(CLOCK), .clr(CLEAR));
  and and_1 (and_1_out, decoder_1_out0, WRITE_CONTROL);
  and and_2 (and_2_out, decoder_1_out1, WRITE_CONTROL);
  and and_3 (and_3_out, decoder_1_out2, WRITE_CONTROL);
  and and_4 (and_4_out, decoder_1_out3, WRITE_CONTROL);
  and and_5 (and_5_out, decoder_1_out4, WRITE_CONTROL);
  and and_6 (and_6_out, decoder_1_out5, WRITE_CONTROL);
  and and_7 (and_7_out, decoder_1_out6, WRITE_CONTROL);
  and and_8 (and_8_out, decoder_1_out7, WRITE_CONTROL);
  and and_9 (and_9_out, decoder_1_out8, WRITE_CONTROL);
  and and_10 (and_10_out, decoder_1_out9, WRITE_CONTROL);
  and and_11 (and_11_out, decoder_1_out10, WRITE_CONTROL);
  Register #(.width(22)) _1 (.D(DATA_WRITE), .en(and_2_out), .Q(_1_q), .clk(CLOCK), .clr(CLEAR));
  Register #(.width(22)) _2 (.D(DATA_WRITE), .en(and_3_out), .Q(_2_q), .clk(CLOCK), .clr(CLEAR));
  Register #(.width(22)) _3 (.D(DATA_WRITE), .en(and_4_out), .Q(_3_q), .clk(CLOCK), .clr(CLEAR));
  Register #(.width(22)) _4 (.D(DATA_WRITE), .en(and_5_out), .Q(_4_q), .clk(CLOCK), .clr(CLEAR));
  Register #(.width(22)) _5 (.D(DATA_WRITE), .en(and_6_out), .Q(_5_q), .clk(CLOCK), .clr(CLEAR));
  Register #(.width(22)) _6 (.D(DATA_WRITE), .en(and_7_out), .Q(_6_q), .clk(CLOCK), .clr(CLEAR));
  Register #(.width(22)) _7 (.D(DATA_WRITE), .en(and_8_out), .Q(_7_q), .clk(CLOCK), .clr(CLEAR));
  Register #(.width(22)) _8 (.D(DATA_WRITE), .en(and_9_out), .Q(_8_q), .clk(CLOCK), .clr(CLEAR));
  Register #(.width(22)) _9 (.D(DATA_WRITE), .en(and_10_out), .Q(_9_q), .clk(CLOCK), .clr(CLEAR));
  Register #(.width(22)) _10 (.D(DATA_WRITE), .en(and_11_out), .Q(_10_q), .clk(CLOCK), .clr(CLEAR));
  and and_12 (and_12_out, decoder_1_out11, WRITE_CONTROL);
  and and_13 (and_13_out, decoder_1_out12, WRITE_CONTROL);
  and and_14 (and_14_out, decoder_1_out13, WRITE_CONTROL);
  and and_15 (and_15_out, decoder_1_out14, WRITE_CONTROL);
  and and_16 (and_16_out, decoder_1_out15, WRITE_CONTROL);
  and and_17 (and_17_out, decoder_1_out16, WRITE_CONTROL);
  and and_18 (and_18_out, decoder_1_out17, WRITE_CONTROL);
  and and_19 (and_19_out, decoder_1_out18, WRITE_CONTROL);
  and and_20 (and_20_out, decoder_1_out19, WRITE_CONTROL);
  and and_21 (and_21_out, decoder_1_out20, WRITE_CONTROL);
  and and_22 (and_22_out, decoder_1_out21, WRITE_CONTROL);
  Register #(.width(22)) _11 (.en(and_12_out), .Q(_11_q), .clk(CLOCK), .clr(CLEAR));  // open: D
  Register #(.width(22)) _12 (.en(and_13_out), .Q(_12_q), .clk(CLOCK), .clr(CLEAR));  // open: D
  Register #(.width(22)) _13 (.en(and_14_out), .Q(_13_q), .clk(CLOCK), .clr(CLEAR));  // open: D
  Register #(.width(22)) _14 (.en(and_15_out), .Q(_14_q), .clk(CLOCK), .clr(CLEAR));  // open: D
  Register #(.width(22)) _15 (.en(and_16_out), .Q(_15_q), .clk(CLOCK), .clr(CLEAR));  // open: D
  Register #(.width(22)) _16 (.en(and_17_out), .Q(_16_q), .clk(CLOCK), .clr(CLEAR));  // open: D
  Register #(.width(22)) _17 (.en(and_18_out), .Q(_17_q), .clk(CLOCK), .clr(CLEAR));  // open: D
  Register #(.width(22)) _18 (.en(and_19_out), .Q(_18_q), .clk(CLOCK), .clr(CLEAR));  // open: D
  Register #(.width(22)) _19 (.en(and_20_out), .Q(_19_q), .clk(CLOCK), .clr(CLEAR));  // open: D
  Register #(.width(22)) _20 (.en(and_21_out), .Q(_20_q), .clk(CLOCK), .clr(CLEAR));  // open: D
  Register #(.width(22)) _21 (.en(and_22_out), .Q(_21_q), .clk(CLOCK), .clr(CLEAR));  // open: D
  Multiplexer #(.select(5), .width(22), .enable("false")) multiplexer_1 (
    .in0(_0_q), .in1(_1_q), .in2(_2_q), .in3(_3_q), .in4(_4_q), .in5(_5_q), .in6(_6_q), .in7(_7_q),
    .in8(_8_q), .in9(_9_q), .in10(_10_q), .in11(_11_q), .in12(_12_q), .in13(_13_q), .in14(_14_q),
    .in15(_15_q), .in16(_16_q), .in17(_17_q), .in18(_18_q), .in19(_19_q), .in20(_20_q), .in21(_21_q),
    .out(READ_DATA_1), .sel(DATA_REGISTER_1));  // open: in22, in23, in24, in25, in26, in27, in28, in29, in30, in31
  Multiplexer #(.select(5), .width(22), .enable("false")) multiplexer_2 (
    .in0(_0_q), .in1(_1_q), .in2(_2_q), .in3(_3_q), .in4(_4_q), .in5(_5_q), .in6(_6_q), .in7(_7_q),
    .in8(_8_q), .in9(_9_q), .in10(_10_q), .in11(_11_q), .in12(_12_q), .in13(_13_q), .in14(_14_q),
    .in15(_15_q), .in16(_16_q), .in17(_17_q), .in18(_18_q), .in19(_19_q), .in20(_20_q), .in21(_21_q),
    .out(READ_DATA_2), .sel(DATA_REGISTER_2));  // open: in22, in23, in24, in25, in26, in27, in28, in29, in30, in31
endmodule

module _22_BIT_ALU (
  input  [21:0] A,
  input  [21:0] B,
  input  [3:0] in_3,
  input  [2:0] in_4,
  input  [1:0] in_5,
  output add_ovf,
  output BEQ,
  output sub_ovf,
  output BNE,
  output [21:0] OUT
);

  wire comparator_1_lt;
  wire [2:0] alu_control_1_pin0;
  wire [4:0] bit_extender_1_out;
  wire [21:0] adder_1_out, adder_2_out, and_1_out, bit_extender_2_out, NOR_out, not_1_out, or_1_out,
       shifter_1_out, shifter_2_out;

  assign not_1_out = ~B;  // NOT_Gate not_1, 22 bits wide
  assign bit_extender_1_out = {{4{1'b0}}, 1'b1};  // Bit_Extender bit_extender_1
  Adder #(.width(22)) adder_1 (.a(A), .b(not_1_out), .out(adder_1_out), .cin(1'b1), .cout(sub_ovf));
  assign and_1_out = A & B;  // AND_Gate and_1, 22 bits wide
  assign or_1_out = A | B;  // OR_Gate or_1, 22 bits wide
  assign NOR_out = ~(A | B);  // NOR_Gate NOR, 22 bits wide
  Comparator #(.width(22), .mode("unsigned")) comparator_1 (.a(A), .b(B), .eq(BEQ), .lt(comparator_1_lt));  // open: gt
  Shifter #(.width(22)) shifter_1 (.in(A), .\dist (bit_extender_1_out), .out(shifter_1_out));
  Shifter #(.width(22), .shift("lr")) shifter_2 (.in(A), .\dist (bit_extender_1_out), .out(shifter_2_out));
  Adder #(.width(22)) adder_2 (.a(A), .b(B), .out(adder_2_out), .cin(1'b0), .cout(add_ovf));
  assign bit_extender_2_out = {{21{1'b0}}, comparator_1_lt};  // Bit_Extender bit_extender_2
  not not_2 (BNE, BEQ);
  ALU_CONTROL alu_control_1 (
    .in_3(in_3), .PIN0(alu_control_1_pin0[0]), .pin1(alu_control_1_pin0[1]), .pin2(alu_control_1_pin0[2]),
    .in_2(in_5), .OPCODE(in_4));
  Multiplexer #(.select(3), .width(22), .enable("false")) multiplexer_1 (
    .in0(adder_2_out), .in1(adder_1_out), .in2(and_1_out), .in3(or_1_out), .in4(NOR_out),
    .in5(bit_extender_2_out), .in6(shifter_1_out), .in7(shifter_2_out), .out(OUT), .sel(alu_control_1_pin0));

  // Notes on the sheet:
  //   AND
  //   OR
  //   SLT
  //   SLL
  //   SRL
  //   0 sub 
endmodule

module ALU_CONTROL (
  input  [2:0] OPCODE,
  input  [1:0] in_2,
  input  [3:0] in_3,
  output PIN0,
  output pin1,
  output pin2
);

  wire and_1_out, and_2_out, and_3_out, and_4_out, and_5_out, and_6_out, and_7_out, and_8_out,
       decoder_1_out0, decoder_1_out1, decoder_1_out2, decoder_1_out3, decoder_1_out4, decoder_1_out5,
       decoder_1_out6, decoder_1_out7, decoder_1_out8, decoder_1_out9, decoder_1_out10, decoder_1_out11,
       decoder_1_out12, decoder_1_out13, decoder_1_out14, decoder_1_out15, decoder_2_out0, decoder_2_out1,
       decoder_2_out2, decoder_2_out3, decoder_2_out4, decoder_2_out5, decoder_2_out6, decoder_2_out7,
       decoder_3_out0, decoder_3_out1, decoder_3_out2, decoder_3_out3;

  Decoder #(.select(4), .enable("false")) decoder_1 (
    .out0(decoder_1_out0), .out1(decoder_1_out1), .out2(decoder_1_out2), .out3(decoder_1_out3),
    .out4(decoder_1_out4), .out5(decoder_1_out5), .out6(decoder_1_out6), .out7(decoder_1_out7),
    .out8(decoder_1_out8), .out9(decoder_1_out9), .out10(decoder_1_out10), .out11(decoder_1_out11),
    .out12(decoder_1_out12), .out13(decoder_1_out13), .out14(decoder_1_out14), .out15(decoder_1_out15),
    .sel(in_3));
  Decoder #(.select(3), .enable("false")) decoder_2 (
    .out0(decoder_2_out0), .out1(decoder_2_out1), .out2(decoder_2_out2), .out3(decoder_2_out3),
    .out4(decoder_2_out4), .out5(decoder_2_out5), .out6(decoder_2_out6), .out7(decoder_2_out7), .sel(OPCODE));
  and and_1 (and_1_out, decoder_1_out4, decoder_2_out0, decoder_3_out1);
  and and_2 (and_2_out, decoder_3_out1, decoder_2_out0, decoder_1_out1);
  and and_3 (and_3_out, decoder_1_out5, decoder_2_out0, decoder_3_out1);
  and and_4 (and_4_out, decoder_1_out6, decoder_2_out0, decoder_3_out1);
  and and_5 (and_5_out, decoder_1_out8, decoder_2_out0, decoder_3_out1);
  and and_6 (and_6_out, decoder_3_out3, decoder_2_out1);
  and and_7 (and_7_out, decoder_3_out1, decoder_2_out0, decoder_1_out2);
  and and_8 (and_8_out, decoder_3_out1, decoder_2_out0, decoder_1_out3);
  Decoder #(.select(2), .enable("false")) decoder_3 (
    .out0(decoder_3_out0), .out1(decoder_3_out1), .out2(decoder_3_out2), .out3(decoder_3_out3), .sel(in_2));
  or or_1 (PIN0, and_8_out, and_3_out, and_4_out, and_5_out);
  or or_2 (pin1, and_7_out, and_1_out, and_4_out, and_5_out);
  or or_3 (pin2, and_2_out, and_1_out, and_3_out, and_4_out);

  // Notes on the sheet:
  //   FUNCTION BITS SELECTION
  //   Function Bits
  //   SLL
  //   NOR
  //   SLT
  //   SRL
  //   OR
  //   BEQ
  //   AND
  //   SUB
  //   ALU OP
  //   ALU OP selection
  //   1
  //   2
  //   4
endmodule

module CONTROL_UNIT (
  input  [2:0] OPCODE,
  output Reg_Dest,
  output Reg_Write,
  output ALU_SRC,
  output MEMRead,
  output MEMWrite,
  output Mem_To_Reg,
  output Jump,
  output Branch,
  output [1:0] ALUOP
);

  wire decoder_1_out0, decoder_1_out1, decoder_1_out2, decoder_1_out5, decoder_1_out7;

  Decoder #(.select(3), .enable("false")) decoder_1 (
    .out0(decoder_1_out0), .out1(decoder_1_out1), .out2(decoder_1_out2), .out3(Mem_To_Reg), .out4(MEMWrite),
    .out5(decoder_1_out5), .out6(Jump), .out7(decoder_1_out7), .sel(OPCODE));
  or or_1 (ALUOP[1], decoder_1_out1, decoder_1_out2, Mem_To_Reg);
  or or_2 (ALUOP[0], decoder_1_out1, decoder_1_out0);
  or or_3 (ALU_SRC, decoder_1_out2, Mem_To_Reg, MEMWrite);
  or or_4 (Branch, decoder_1_out1, decoder_1_out5);
  buf or_5 (Reg_Dest, decoder_1_out0);  // OR_Gate
  or or_6 (Reg_Write, decoder_1_out0, decoder_1_out2, Mem_To_Reg);

  assign MEMRead = Mem_To_Reg;
endmodule

module _22_MIPS_DATAPATH (
  input  in_1,
  input  in_2,
  output [4:0] out_3,
  output [21:0] out_4,
  output [4:0] out_5,
  output [21:0] out_6,
  output [21:0] out_7,
  output [21:0] out_8
);

  wire and_1_out, and_2_out, clock_1_out, control_unit_1_alu_src, control_unit_1_branch, control_unit_1_jump,
       control_unit_1_mem_to_reg, control_unit_1_memread, control_unit_1_memwrite, control_unit_1_reg_dest,
       control_unit_1_reg_write, n22_bit_alu_1_beq, n22_bit_alu_1_bne, or_1_out;
  wire [1:0] control_unit_1_aluop;
  wire [4:0] multiplexer_1_out;
  wire [21:0] adder_1_out, adder_2_out, bit_extender_1_out, bit_extender_2_out, bit_extender_3_out,
       multiplexer_2_out, multiplexer_3_out, multiplexer_4_out, ram_1_data, register_1_q, rom_1_data;

  Clock clock_1 (.out(clock_1_out));
  assign bit_extender_1_out = {{21{1'b0}}, 1'b1};  // Bit_Extender bit_extender_1
  Register #(.width(22)) register_1 (
    .D(multiplexer_4_out), .Q(register_1_q), .clk(clock_1_out), .clr(in_2));  // open: en
  Adder #(.width(22)) adder_1 (.a(bit_extender_1_out), .b(register_1_q), .out(adder_1_out));  // open: cin, cout
  ROM #(.addrWidth(22), .dataWidth(22)) rom_1 (
    .addr(register_1_q), .data({rom_1_data[21:19], out_3, out_5, rom_1_data[8:0]}));  // open: sel
  assign bit_extender_2_out = {{3{1'b0}}, {out_3, out_5, rom_1_data[8:0]}};  // Bit_Extender bit_extender_2
  assign bit_extender_3_out = {{13{1'b0}}, rom_1_data[8:0]};  // Bit_Extender bit_extender_3
  Multiplexer #(.width(5), .enable("false")) multiplexer_1 (
    .in0(out_5), .in1(rom_1_data[8:4]), .out(multiplexer_1_out), .sel(control_unit_1_reg_dest));
  _22_BIT_REGISTER u_22_bit_register_1 (
    .READ_DATA_1(out_4), .READ_DATA_2(out_6), .WRITE_REGISTER(multiplexer_1_out),
    .WRITE_CONTROL(control_unit_1_reg_write), .DATA_WRITE(out_8), .CLOCK(clock_1_out),
    .DATA_REGISTER_1(out_3), .DATA_REGISTER_2(out_5));  // open: CLEAR
  CONTROL_UNIT control_unit_1 (
    .OPCODE(rom_1_data[21:19]), .Reg_Dest(control_unit_1_reg_dest), .Reg_Write(control_unit_1_reg_write),
    .MEMRead(control_unit_1_memread), .MEMWrite(control_unit_1_memwrite),
    .Mem_To_Reg(control_unit_1_mem_to_reg), .Jump(control_unit_1_jump), .Branch(control_unit_1_branch),
    .ALUOP(control_unit_1_aluop), .ALU_SRC(control_unit_1_alu_src));
  Adder #(.width(22)) adder_2 (.a(adder_1_out), .b(bit_extender_3_out), .out(adder_2_out));  // open: cin, cout
  Multiplexer #(.width(22), .enable("false")) multiplexer_2 (
    .in0(out_6), .in1(bit_extender_3_out), .out(multiplexer_2_out), .sel(control_unit_1_alu_src));
  _22_BIT_ALU u_22_bit_alu_1 (
    .in_3(rom_1_data[3:0]), .in_5(control_unit_1_aluop), .OUT(out_7), .A(out_4), .B(multiplexer_2_out),
    .BEQ(n22_bit_alu_1_beq), .BNE(n22_bit_alu_1_bne), .in_4(rom_1_data[21:19]));  // open: add_ovf, sub_ovf
  or or_1 (or_1_out, and_1_out, and_2_out);
  and and_1 (and_1_out, n22_bit_alu_1_beq, control_unit_1_branch);
  and and_2 (and_2_out, n22_bit_alu_1_bne, control_unit_1_branch);
  Multiplexer #(.width(22), .enable("false")) multiplexer_3 (
    .in0(adder_1_out), .in1(adder_2_out), .out(multiplexer_3_out), .sel(or_1_out));
  Multiplexer #(.width(22), .enable("false")) multiplexer_4 (
    .in0(multiplexer_3_out), .in1(bit_extender_2_out), .out(multiplexer_4_out), .sel(control_unit_1_jump));
  RAM #(.addrWidth(22), .dataWidth(22), .bus("separate")) ram_1 (
    .addr(out_7), .din(out_6), .data(ram_1_data), .str(control_unit_1_memwrite), .clk(clock_1_out),
    .ld(control_unit_1_memread), .clr(in_1));  // open: sel
  Multiplexer #(.width(22), .enable("false")) multiplexer_5 (
    .in0(out_7), .in1(ram_1_data), .out(out_8), .sel(control_unit_1_mem_to_reg));

  // Notes on the sheet:
  //   CLOCK
  //   contents of rom_1 (hex, n*v repeats v):
  //   10040a 100602 8647 200802
  //   ADDRESS
  //   IMMEDIATE VALUE
  //   FUNCTION BITS
  //   RD
  //   RT
  //   RS
  //   OPCODE
endmodule
